// Digital circuit hardware.dig as structural Verilog
module hardware (
  input  clk,
  input  in_2,
  input  [3:0] in_3,
  input  [3:0] in_4,
  input  [3:0] in_5,
  input  [3:0] in_6,
  input  in_7,
  input  [15:0] in_8,
  input  in_9,
  input  in_10,
  input  in_11,
  input  [15:0] in_12,
  input  in_13,
  input  [15:0] in_14,
  input  in_15,
  input  in_16,
  input  [15:0] in_17
);

  wire alu_1_fn, PC_ovf;
  wire [15:0] InstrReg_q, PC_out, ramdualport_1_d, registerfile_1_da, registerfile_1_db;

  RegisterFile #(.AddrBits(4), .Bits(16)) registerfile_1 (
    .Din(in_8), .we(in_2), .Rw(in_3), .C(clk), .Ra(in_4), .Rb(in_5), .Da(registerfile_1_da),
    .Db(registerfile_1_db));
  CounterPreset #(.Bits(16)) PC (
    .en(in_9), .C(clk), .dir(in_10), .in(in_12), .ld(in_11), .clr(in_13), .out(PC_out), .ovf(PC_ovf));
  // Probe on PC_out
  // Probe on PC_ovf
  alu alu_1 (.Op(in_6), .TData(registerfile_1_da), .AData(registerfile_1_db), .fN(alu_1_fn));  // open: RData, fZ, fC
  RAMDualPort #(.AddrBits(16), .Bits(16)) ramdualport_1 (
    .A(in_14), .Din(in_17), .str(in_15), .C(clk), .ld(in_16), .D(ramdualport_1_d));
  // Probe on alu_1_fn
  Register #(.Bits(16)) InstrReg (.D(ramdualport_1_d), .C(clk), .en(in_7), .Q(InstrReg_q));
  // Probe on InstrReg_q
endmodule
